// Logisim project alu.circ as structural Verilog: 1 circuit, main circuit alu
module alu (
  input  [31:0] A,
  input  [31:0] B,
  input  [3:0] ALUSel,
  output [31:0] Result
);

  wire and_2_out, msbN, xor_2_out, xor_3_out, xor_4_out;
  wire [4:0] bit_extender_1_out, bit_extender_2_out, bit_extender_3_out;
  wire [30:0] sub0;
  wire [31:0] add0, and0, mul0, mulh0, mulhu0, or0, sll0, slt0, sra0, srl0, xor0;

  Adder #(.width(32)) adder_1 (.a(A), .b(B), .out(add0));  // open: cin, cout
  assign and0 = A & B;  // AND_Gate and_1, 32 bits wide
  assign or0 = A | B;  // OR_Gate or_1, 32 bits wide
  assign xor0 = A ^ B;  // XOR_Gate xor_1, 32 bits wide
  Bit_Extender #(.in_width(32), .out_width(5)) bit_extender_1 (.in(B), .out(bit_extender_1_out));
  Bit_Extender #(.in_width(32), .out_width(5)) bit_extender_2 (.in(B), .out(bit_extender_2_out));
  Bit_Extender #(.in_width(32), .out_width(5)) bit_extender_3 (.in(B), .out(bit_extender_3_out));
  Multiplier #(.mode("twosComplement"), .width(32)) multiplier_1 (.a(A), .b(B), .out(mul0), .cout(mulh0));  // open: cin
  Multiplier #(.width(32)) multiplier_2 (.a(A), .b(B), .cout(mulhu0));  // open: out, cin
  xor xor_2 (xor_2_out, A[31], B[31]);
  xor xor_3 (xor_3_out, A[31], msbN);
  Shifter #(.shift("lr"), .width(32)) shifter_1 (.in(A), .\dist (bit_extender_1_out), .out(srl0));
  Shifter #(.shift("ar"), .width(32)) shifter_2 (.in(A), .\dist (bit_extender_2_out), .out(sra0));
  Shifter #(.width(32)) shifter_3 (.in(A), .\dist (bit_extender_3_out), .out(sll0));
  Subtractor #(.width(32)) subtractor_1 (.a(A), .b(B), .out({msbN, sub0}));  // open: bin, bout
  and and_2 (and_2_out, xor_2_out, xor_3_out);
  assign slt0 = {{31{1'b0}}, xor_4_out};  // Bit_Extender bit_extender_4
  xor xor_4 (xor_4_out, and_2_out, msbN);
  Multiplexer #(.enable("false"), .select(4), .width(32)) multiplexer_1 (
    .in0(add0), .in1(and0), .in2(or0), .in3(xor0), .in4(srl0), .in5(sra0), .in6(sll0), .in7(slt0),
    .in10(mul0), .in11(mulhu0), .in12({msbN, sub0}), .in13(B), .in14(mulh0), .out(Result), .sel(ALUSel));  // open: in8, in9, in15

  // Other names for the same wires on the sheet: msbA = A[31]; bsel0[31:0] = B; msbB = B[31]; sub0[31] = msbN

  // Notes on the sheet:
  //   INPUTS to your circuit
  //   DON'T CHANGE THE LOCATIONS OF THE INPUTS AND OUTPUTS!
  //   OUTPUT from your circuit
endmodule
