// Logisim project regfile.circ as structural Verilog: 1 circuit, main circuit regfile
module regfile (
  input  [4:0] rs1,
  input  [4:0] rs2,
  input  [4:0] rd,
  input  [31:0] Write_Data,
  input  RegWEn,
  input  clk,
  output [31:0] ra,
  output [31:0] sp,
  output [31:0] t0,
  output [31:0] t1,
  output [31:0] t2,
  output [31:0] s0,
  output [31:0] s1,
  output [31:0] a0,
  output [31:0] Read_Data_1,
  output [31:0] Read_Data_2
);

  wire write_a0, write_ra, write_s0, write_s1, write_sp, write_t0, write_t1, write_t2;
  wire [31:0] x0;

  Register #(.width(32)) register_1 (.clk(clk), .Q(x0), .clr(1'b1));  // open: D, en
  Register #(.width(32)) register_2 (.D(Write_Data), .en(write_ra), .clk(clk), .Q(ra));  // open: clr
  Register #(.width(32)) register_3 (.D(Write_Data), .en(write_sp), .clk(clk), .Q(sp));  // open: clr
  Register #(.width(32)) register_4 (.D(Write_Data), .en(write_t0), .clk(clk), .Q(t0));  // open: clr
  Register #(.width(32)) register_5 (.D(Write_Data), .en(write_t1), .clk(clk), .Q(t1));  // open: clr
  Register #(.width(32)) register_6 (.D(Write_Data), .en(write_t2), .clk(clk), .Q(t2));  // open: clr
  Register #(.width(32)) register_7 (.D(Write_Data), .en(write_s0), .clk(clk), .Q(s0));  // open: clr
  Register #(.width(32)) register_8 (.D(Write_Data), .en(write_s1), .clk(clk), .Q(s1));  // open: clr
  Register #(.width(32)) register_9 (.D(Write_Data), .en(write_a0), .clk(clk), .Q(a0));  // open: clr
  Multiplexer #(.enable("false"), .select(5), .width(32)) multiplexer_1 (
    .in0(x0), .in1(ra), .in2(sp), .in5(t0), .in6(t1), .in7(t2), .in8(s0), .in9(s1), .in10(a0),
    .out(Read_Data_1), .sel(rs1));  // open: in3, in4, in11, in12, in13, in14, in15, in16, in17, in18, in19, in20, in21, in22, in23, in24, in25, in26, in27, in28, in29, in30, in31
  Multiplexer #(.enable("false"), .select(5), .width(32)) multiplexer_2 (
    .in0(x0), .in1(ra), .in2(sp), .in5(t0), .in6(t1), .in7(t2), .in8(s0), .in9(s1), .in10(a0),
    .out(Read_Data_2), .sel(rs2));  // open: in3, in4, in11, in12, in13, in14, in15, in16, in17, in18, in19, in20, in21, in22, in23, in24, in25, in26, in27, in28, in29, in30, in31
  Demultiplexer #(.enable("false"), .select(5)) demultiplexer_1 (
    .out1(write_ra), .out2(write_sp), .out5(write_t0), .out6(write_t1), .out7(write_t2), .out8(write_s0),
    .out9(write_s1), .out10(write_a0), .in(RegWEn), .sel(rd));  // open: out0, out3, out4, out11, out12, out13, out14, out15, out16, out17, out18, out19, out20, out21, out22, out23, out24, out25, out26, out27, out28, out29, out30, out31

  // Other names for the same wires on the sheet: read_data1[31:0] = Read_Data_1; read_data2[31:0] = Read_Data_2;
  //   read_reg1[4:0] = rs1; read_reg2[4:0] = rs2; write_en = RegWEn; write_reg[4:0] = rd

  // Notes on the sheet:
  //   INPUTS to your circuit
  //   DON'T CHANGE THE LOCATIONS OF THE INPUTS AND OUTPUTS!
  //   These are DEBUG/TEST outputs from your circuit.
  //   OUTPUTS from your circuit
endmodule
